// Digital circuit Original Chipset.dig as structural Verilog
module Original_Chipset (
  input  A11,
  input  A12,
  input  A13,
  input  A14,
  input  A15,
  input  nMREQ,
  input  nRD,
  input  nWR,
  output nMMIORD__6800_6FFF,
  output nMMIOWR_6800_6FFF,
  output nVIDRWR__7000_77FF,
  output n2KVIDR__7000_77FF,
  output nRAM0__7800_7FFF,
  output nRAM1__8000_87FF,
  output RAM2__8800_8FFF,
  output nROM00__0000_1FFF,
  output nROM01__2000_3FFF
);

  wire n2KMMIO__6800_6FFF, n2KRNG__6000_7FFF, nand_1_out, or_1_out;
  wire [2:0] delay_1_out;

  or or_1 (or_1_out, A15, nMREQ);
  Demultiplexer #(.Selector_Bits(2), .Default(1)) demultiplexer_1 (
    .sel({A14, A13}), .in(or_1_out), .out_0(nROM00__0000_1FFF), .out_1(nROM01__2000_3FFF),
    .out_3(n2KRNG__6000_7FFF));  // open: out_2
  nand nand_1 (nand_1_out, A15, ~A14, ~nMREQ);  // NAnd
  Demultiplexer #(.Selector_Bits(2), .Default(1)) demultiplexer_2 (
    .sel({A12, A11}), .in(n2KRNG__6000_7FFF), .out_1(n2KMMIO__6800_6FFF), .out_2(n2KVIDR__7000_77FF),
    .out_3(nRAM0__7800_7FFF));  // open: out_0
  Demultiplexer #(.Selector_Bits(3), .Default(1)) demultiplexer_3 (
    .sel(delay_1_out), .in(nand_1_out), .out_0(nRAM1__8000_87FF), .out_1(RAM2__8800_8FFF));  // open: out_2, out_3, out_4, out_5, out_6, out_7
  Delay #(.Bits(3)) delay_1 (.in({A13, A12, A11}), .out(delay_1_out));
  or or_2 (nMMIORD__6800_6FFF, nRD, n2KMMIO__6800_6FFF);
  or or_3 (nMMIOWR_6800_6FFF, n2KMMIO__6800_6FFF, nWR);
  or or_4 (nVIDRWR__7000_77FF, nWR, n2KVIDR__7000_77FF);

  // Other names for the same wires on the sheet: A11__PIN_1 = A11; A12__PIN_2 = A12; A13__PIN_3 = A13;
  //   A14__PIN_5 = A14; A15__PIN_6 = A15; n2KRAM0__7800_7FFF = nRAM0__7800_7FFF;
  //   n2KRAM1__8000_87FF = nRAM1__8000_87FF; n2KRAM2__8800_8FFF = RAM2__8800_8FFF; nMREQ__PIN_4 = nMREQ

  // Notes on the sheet:
  //   nRAM0__7800_7FFF: ~RAM (7800-7FFF)
  //   Additional 2K decode Ranges (8000-BFFF ONLY)
  //   INTERNAL TO 74LS138
  //   8K Decode Ranges
  //   2K Decode Ranges
  //   Memory Mapped IO
  //   BUFF. & /MS ON VDG (GATE BY /WR ON BUFF)
  //   FASTER THAN /VIDRWR BY 1 GATE DELAY
  //   CHIPSET CAN NOT SELECT RAM IN C000-FFFF
  //   2K VID RAM /WR (+1 GATE DELAY)
endmodule
