// Digital circuit Banking GAL.dig as structural Verilog
module Banking_GAL (
  input  nIOWRI,
  input  A7,
  input  A6,
  input  A5,
  input  A4,
  input  D3,
  input  D0,
  input  D1,
  input  D2,
  input  nBANK,
  input  A15,
  input  A14,
  output BA16,
  output BA15,
  output BA14,
  output CFG10K
);

  wire _70to7F, b14, b15, b16, multiplexer_1_out, multiplexer_2_out, multiplexer_3_out, multiplexer_4_out;

  and and_1 (_70to7F, ~A7, A6, A5, A4);  // And
  Multiplexer multiplexer_1 (.sel(_70to7F), .in_0(b14), .in_1(D0), .out(multiplexer_1_out));
  Multiplexer multiplexer_2 (.sel(_70to7F), .in_0(b15), .in_1(D1), .out(multiplexer_2_out));
  Multiplexer multiplexer_3 (.sel(_70to7F), .in_0(b16), .in_1(D2), .out(multiplexer_3_out));
  Multiplexer multiplexer_4 (.sel(_70to7F), .in_0(CFG10K), .in_1(D3), .out(multiplexer_4_out));
  D_FF d_ff_1 (.D(multiplexer_1_out), .C(nIOWRI), .Q(b14));  // open: nQ
  D_FF d_ff_2 (.D(multiplexer_2_out), .C(nIOWRI), .Q(b15));  // open: nQ
  D_FF d_ff_3 (.D(multiplexer_3_out), .C(nIOWRI), .Q(b16));  // open: nQ
  D_FF d_ff_4 (.D(multiplexer_4_out), .C(nIOWRI), .Q(CFG10K));  // open: nQ
  Multiplexer multiplexer_5 (.sel(nBANK), .in_0(b15), .in_1(A15), .out(BA15));
  Multiplexer multiplexer_6 (.sel(nBANK), .in_0(b14), .in_1(A14), .out(BA14));
  Multiplexer multiplexer_7 (.sel(nBANK), .in_0(b16), .in_1(1'b0), .out(BA16));

  // Other names for the same wires on the sheet: _10KBANK = CFG10K

  // Notes on the sheet:
  //   nIOWRI: pin 1
  //   A7: pin 2
  //   A6: pin 3
  //   A5: pin 4
  //   A4: pin 5
  //   D3: pin 9
  //   D0: pin 10
  //   D1: pin 11
  //   D2: pin 13
  //   nBANK: pin 6
  //   BA16: pin 23
  //   BA15: pin 22
  //   BA14: pin 21
  //   A15: pin 7
  //   A14: pin 8
  //   CFG10K: pin 20
endmodule
