// Digital circuit Decode Logic.dig as structural Verilog
module Decode_Logic (
  input  A15,
  input  A14,
  input  A13,
  input  A12,
  input  A11,
  input  nWR,
  input  nMREQ,
  input  nM1,
  input  nIOREQ,
  input  CFG10K,
  output IOWRI,
  output nBANK,
  output nRAM,
  output nROM
);

  wire _4000to67FF, and_2_out, and_3_out, demultiplexer_1_out_0, demultiplexer_1_out_1,
       demultiplexer_1_out_3, demultiplexer_2_out_3, demultiplexer_3_out_0, demultiplexer_3_out_1,
       demultiplexer_3_out_2, demultiplexer_3_out_3, demultiplexer_3_out_4, MREQ15, nand_1_out, not_1_out,
       not_2_out, or_2_out, or_3_out;

  or or_1 (MREQ15, nMREQ, A15);
  not not_1 (not_1_out, nWR);
  not not_2 (not_2_out, nIOREQ);
  Demultiplexer #(.Selector_Bits(2), .Default(1)) demultiplexer_1 (
    .sel({A14, A13}), .in(MREQ15), .out_0(demultiplexer_1_out_0), .out_1(demultiplexer_1_out_1),
    .out_3(demultiplexer_1_out_3));  // open: out_2
  nand nand_1 (nand_1_out, ~MREQ15, A14);  // NAnd
  and and_1 (IOWRI, nM1, not_1_out, not_2_out);
  or or_2 (or_2_out, CFG10K, _4000to67FF);
  and and_2 (and_2_out, demultiplexer_1_out_0, demultiplexer_1_out_1);
  Demultiplexer #(.Selector_Bits(2), .Default(1)) demultiplexer_2 (
    .sel({A12, A11}), .in(demultiplexer_1_out_3), .out_3(demultiplexer_2_out_3));  // open: out_0, out_1, out_2
  Demultiplexer #(.Selector_Bits(3), .Default(1)) demultiplexer_3 (
    .sel({A13, A12, A11}), .in(nand_1_out), .out_0(demultiplexer_3_out_0), .out_1(demultiplexer_3_out_1),
    .out_2(demultiplexer_3_out_2), .out_3(demultiplexer_3_out_3), .out_4(demultiplexer_3_out_4));  // open: out_5, out_6, out_7
  and and_3 (and_3_out, A15, ~nMREQ);  // And
  and and_4 (_4000to67FF, demultiplexer_3_out_0, demultiplexer_3_out_1, demultiplexer_3_out_2, demultiplexer_3_out_3, demultiplexer_3_out_4);
  and and_5 (nROM, or_2_out, and_2_out);
  nand nand_2 (nBANK, A15, A14);
  or or_3 (or_3_out, ~CFG10K, _4000to67FF);  // Or
  and and_6 (nRAM, ~and_3_out, demultiplexer_2_out_3, or_3_out);  // And

  // Notes on the sheet:
  //   A15: pin 1
  //   A14: pin 2
  //   A13: pin 3
  //   A12: pin 4
  //   A11: pin 5
  //   nWR: pin 9
  //   nMREQ: pin 10
  //   nM1: pin 11
  //   nIOREQ: pin 13
  //   IOWRI: pin 23
  //   nBANK: pin 22
  //   nRAM: pin 18
  //   nROM: pin 17
  //   CFG10K: pin 6
endmodule
