// Digital circuit Serial Card Gal.dig as structural Verilog
module Serial_Card_Gal (
  input  UARTCLK,
  input  A7,
  input  A6,
  input  A5,
  input  A4,
  input  TX,
  input  RX,
  input  M1,
  input  nIOREQ,
  input  IRQ,
  output RTS,
  output RXLED,
  output TXLED,
  output SCLK,
  output E,
  output nIODEC
);

  wire and_1_out, d_ff_1_q, Div4;

  and and_1 (and_1_out, A7, M1, ~A6, ~A5, ~A4);  // And
  D_FF d_ff_1 (.D(Div4), .C(UARTCLK), .Q(d_ff_1_q));  // open: nQ
  not not_1 (RTS, IRQ);
  not not_2 (RXLED, TX);
  not not_3 (TXLED, RX);
  not not_4 (nIODEC, and_1_out);
  not not_5 (E, nIOREQ);
  D_FF d_ff_2 (.D(d_ff_1_q), .C(UARTCLK), .Q(SCLK), .nQ(Div4));

  // Notes on the sheet:
  //   UARTCLK: pin 1
  //   A7: pin 2
  //   A6: pin 3
  //   A5: pin 4
  //   A4: pin 5
  //   TX: pin 6
  //   RX: pin 7
  //   M1: pin 8
  //   nIOREQ: pin 11
  //   IRQ: pin 13
  //   RTS: pin 23
  //   RXLED: pin 22
  //   TXLED: pin 21
  //   SCLK: pin 20
  //   E: pin 15
  //   nIODEC: pin 14
endmodule
