// Digital circuit VDG Card GAL.dig as structural Verilog
module VDG_Card_GAL (
  input  A11,
  input  A12,
  input  Q,
  input  A13,
  input  A14,
  input  A15,
  input  D4,
  input  D3,
  input  nWR,
  input  nMREQ,
  input  nWT1,
  input  nWT0,
  output nA_G,
  output CSS,
  output nDRAM,
  output nVZIO,
  output INTLATCH,
  output nVDGCE
);

  wire demultiplexer_1_out_3, multiplexer_1_out, multiplexer_2_out, nvwiat, nwait, or_1_out, or_2_out;

  and and_1 (nwait, nWT0, nWT1);
  or or_1 (or_1_out, A15, nMREQ);
  Demultiplexer #(.Selector_Bits(2), .Default(1)) demultiplexer_1 (
    .sel({A14, A13}), .in(or_1_out), .out_3(demultiplexer_1_out_3));  // open: out_0, out_1, out_2
  and and_2 (nVDGCE, ~nDRAM, ~nvwiat, ~nWR);  // And
  Demultiplexer #(.Selector_Bits(2), .Default(1)) demultiplexer_2 (
    .sel({A12, A11}), .in(demultiplexer_1_out_3), .out_1(nVZIO), .out_2(nDRAM));  // open: out_0, out_3
  Multiplexer multiplexer_1 (.sel(or_2_out), .in_0(D4), .in_1(CSS), .out(multiplexer_1_out));
  Multiplexer multiplexer_2 (.sel(or_2_out), .in_0(D3), .in_1(nA_G), .out(multiplexer_2_out));
  or or_2 (or_2_out, nWR, nVZIO);
  D_FF d_ff_1 (.D(multiplexer_1_out), .C(Q), .Q(CSS));  // open: nQ
  D_FF d_ff_2 (.D(multiplexer_2_out), .C(Q), .Q(nA_G));  // open: nQ
  D_FF d_ff_3 (.D(nwait), .C(Q), .Q(nvwiat));  // open: nQ
  nor nor_1 (INTLATCH, nWR, nMREQ);

  // Notes on the sheet:
  //   A11: pin 2
  //   A12: pin 3
  //   Q: pin 1
  //   A13: pin 4
  //   A14: pin 5
  //   A15: pin 6
  //   D4: pin 9
  //   D3: pin 10
  //   nWR: pin 11
  //   nMREQ: pin 13
  //   nA_G: pin 22
  //   CSS: pin 21
  //   nDRAM: pin 20
  //   nVZIO: pin 19
  //   INTLATCH: pin 23
  //   nWT1: pin 7
  //   nWT0: pin 8
  //   nVDGCE: pin 18
endmodule
